# Fritzing sketch PIR_module (saved by Fritzing 1.0.2b)
breadboards: 1

parts:
  Part1 = HC-SR501 Body Sensor Module
  MH-ET_LIVE_ESP32_DEVKIT1 = MH-ET LIVE ESP32 DEVKIT 38 pins

nets:
  VCC: Part1.VCC, MH-ET_LIVE_ESP32_DEVKIT1.3V3
  N1: Part1.OUT, MH-ET_LIVE_ESP32_DEVKIT1.IO4
  GND: Part1.GND, MH-ET_LIVE_ESP32_DEVKIT1.GND

custom parts:
  HC-SR501 Body Sensor Module: Pyroelectric Infrared PIR Motion Sensor Detector Module
  MH-ET LIVE ESP32 DEVKIT 38 pins: http://mh.nodebb.com/topic/2/mh-et-live-esp32-devkit
