# Fritzing sketch TH_module (saved by Fritzing 1.0.2b)
circuit board: 8.46667cm x 5.64444cm
breadboards: 1

parts:
  R1 = Resistor [tolerance=±5% resistance=10k package="2010 [SMD]"]
  Mod1 = KY-015 Temperature & Humidity Sensor Module - DH11 [package="Breakout board"]
  MH-ET_LIVE_ESP32_DEVKIT1 = MH-ET LIVE ESP32 DEVKIT 38 pins

nets:
  VIN: R1.Pin_0, Mod1.Vin, MH-ET_LIVE_ESP32_DEVKIT1.3V3
  N1: R1.Pin_1, Mod1.S, MH-ET_LIVE_ESP32_DEVKIT1.IO4
  N2: Mod1.-, MH-ET_LIVE_ESP32_DEVKIT1.GND

custom parts:
  KY-015 Temperature & Humidity Sensor Module - DH11: KY-015 temperature and humidity sensor module, provides a low-latency serial interface to measure humidity and temperature.
  MH-ET LIVE ESP32 DEVKIT 38 pins: http://mh.nodebb.com/topic/2/mh-et-live-esp32-devkit
