# Fritzing sketch Untitled Sketch (saved by Fritzing 1.0.2b)
breadboards: 1

parts:
  MH-ET_LIVE_ESP32_DEVKIT1 = MH-ET LIVE ESP32 DEVKIT 38 pins
  R1 = Resistor [tolerance=±5% resistance=10k package="2010 [SMD]"]
  Mod1 = KY-015 Temperature & Humidity Sensor Module - DH11 [package="Breakout board"]

nets:
  3V3: MH-ET_LIVE_ESP32_DEVKIT1.3V3, R1.Pin_0, Mod1.Vin
  N1: MH-ET_LIVE_ESP32_DEVKIT1.GND, Mod1.-
  N2: MH-ET_LIVE_ESP32_DEVKIT1.IO4, R1.Pin_1, Mod1.S

custom parts:
  MH-ET LIVE ESP32 DEVKIT 38 pins: http://mh.nodebb.com/topic/2/mh-et-live-esp32-devkit
  KY-015 Temperature & Humidity Sensor Module - DH11: KY-015 temperature and humidity sensor module, provides a low-latency serial interface to measure humidity and temperature.
